// Logisim project KP8B.circ as structural Verilog: 1 circuit, main circuit main
module main (
  input  in_1
);

  wire and_1_out, and_2_out, and_3_out, and_4_out, and_5_out, and_6_out, and_7_out, and_8_out, and_9_out,
       and_10_out, and_11_out, and_12_out, and_13_out, and_14_out, and_16_out, and_17_out, C0, C1, C2, C3,
       C4, C5, C6, C7, CLK, clock_1_out, dipswitch_2_p1, dipswitch_2_p2, Enable, IRQ, keyboard_1_avail,
       KEYREAD, not_1_out, not_2_out, not_3_out, not_4_out, not_6_out, res, sH, sL, TERMINAL, WE;
  wire [3:0] multiplexer_2_out;
  wire [4:0] pla_2_out;
  wire [6:0] KEY;
  wire [7:0] Bin, C6_q, C7_q, DATA, Dh, Dl, multiplexer_1_out, ram_1_dout, rom_1_data, rom_2_data,
       ScreenIn_q, ScreenPos;
  wire [7:7] undriven;
  wire [15:0] kp8b_1_addr;
  wire [23:0] X_q;

  and and_1 (and_1_out, sL, WE);
  and and_2 (and_2_out, sH, WE);
  and and_3 (and_3_out, C0, WE);
  and and_4 (and_4_out, C1, WE);
  and and_5 (and_5_out, C2, WE);
  and and_6 (and_6_out, C3, WE);
  and and_7 (and_7_out, C4, WE);
  and and_8 (and_8_out, C6, WE);
  and and_9 (and_9_out, C7, WE);
  Register Cl (.D(DATA), .en(and_1_out), .clk(CLK), .Q(Dl));  // open: clr
  Register Ch (.D(DATA), .en(and_2_out), .clk(CLK), .Q(Dh));  // open: clr
  Register u_ScreenPos (.D(DATA), .en(and_3_out), .clk(CLK), .Q(ScreenPos));  // open: clr
  Register ScreenIn (.D(DATA), .en(and_4_out), .clk(CLK), .Q(ScreenIn_q));  // open: clr
  Register X (.D(DATA), .en(and_5_out), .clk(CLK), .Q(X_q[7:0]));  // open: clr
  Register Y (.D(DATA), .en(and_6_out), .clk(CLK), .Q(X_q[15:8]));  // open: clr
  Register Z (.D(DATA), .en(and_7_out), .clk(CLK), .Q(X_q[23:16]));  // open: clr
  Register u_C6 (.D(DATA), .en(and_8_out), .clk(CLK), .Q(C6_q));  // open: clr
  Register u_C7 (.D(DATA), .en(and_9_out), .clk(CLK), .Q(C7_q));  // open: clr
  Clock clock_1 (.out(clock_1_out));
  Multiplexer #(.select(4), .width(8)) multiplexer_1 (
    .in0(rom_2_data), .in1(ram_1_dout), .in2({8{1'b0}}), .in3({undriven[7], KEY}), .in4(Dl), .in5(Dh),
    .in6(Bin), .in7(ScreenPos), .in8(ScreenIn_q), .in9(X_q[7:0]), .in10(X_q[15:8]), .in11(X_q[23:16]),
    .in12(rom_1_data), .in13(C6_q), .in14(C7_q), .out(multiplexer_1_out), .sel(multiplexer_2_out));  // open: in15
  Multiplexer #(.width(4)) multiplexer_2 (
    .in0({3'b000, WE}), .in1(pla_2_out[3:0]), .out(multiplexer_2_out), .sel(pla_2_out[4]));
  PLA #(.in_width(4), .out_width(12), .\table ("0101 000000000001 # Sh\n0100 000000000010 # Sl\n0010 000000000100 # Terminal\n0011 000000001000 # Keyread\n0111 000000010000 # Matrix0\n1000 000000100000 # Matrix1\n1001 000001000000 # Matrix2\n1010 000010000000 # Matrix3\n1011 000100000000 # Matrix4\n1100 001000000000 # Matrix5\n1101 010000000000 # Matrix6\n1110 100000000000 # Matrix7")) pla_1 (
    .in(multiplexer_2_out), .out({C7, C6, C5, C4, C3, C2, C1, C0, KEYREAD, TERMINAL, sL, sH}));
  KP8B kp8b_1 (
    .DIN(multiplexer_1_out), .IRQ(IRQ), .NMI(in_1), .RES(res), .RDY(Enable), .CLK(clock_1_out),
    .ADDR(kp8b_1_addr), .R_W(WE), .CLKO(CLK), .DOUT(DATA));  // open: MRB
  PLA #(.in_width(16), .out_width(5), .\table ("1111111111111110 10010 # TERMINAL\n1111111111111111 10011 # KEYBOARD\n1111111111111100 10100 # HEX-LOW\n1111111111111101 10101 # HEX-HIGH\n1111111111111011 10110 # Binary In\n1111111111110011 10111 # C0\n1111111111110100 11000 # C1\n1111111111110101 11001 # C2\n1111111111110110 11010 # C3\n1111111111110111 11011 # C4\n1111111111111000 11100 # C5\n1111111111111001 11101 # C6\n1111111111111010 11110 # C7")) pla_2 (
    .in(kp8b_1_addr), .out(pla_2_out));
  not not_1 (not_1_out, pla_2_out[4]);
  and and_10 (and_10_out, C5, WE);
  ROM #(.addrWidth(24)) rom_1 (.addr(X_q), .data(rom_1_data));
  ROM #(.addrWidth(15)) rom_2 (.addr(kp8b_1_addr[14:0]), .data(rom_2_data));
  RAM #(.addrWidth(15), .enables("line")) ram_1 (
    .addr(kp8b_1_addr[14:0]), .we(and_11_out), .clk(CLK), .din(DATA), .dout(ram_1_dout));
  and and_11 (and_11_out, kp8b_1_addr[15], WE, not_1_out);
  and and_12 (and_12_out, TERMINAL, WE);
  Hex_Digit_Display #(.decimalPoint("false")) hex_digit_display_1 (.value(Dh[7:4]));
  TTY tty_1 (.data(DATA[6:0]), .clk(CLK), .we(and_12_out), .clr(res));
  Keyboard #(.buflen(1)) keyboard_1 (.clk(CLK), .re(and_13_out), .clr(res), .avail(keyboard_1_avail), .data(KEY));
  and and_13 (and_13_out, KEYREAD, ~WE);  // AND_Gate
  Hex_Digit_Display #(.decimalPoint("false")) hex_digit_display_2 (.value(Dh[3:0]));
  Hex_Digit_Display #(.decimalPoint("false")) hex_digit_display_3 (.value(Dl[7:4]));
  and and_14 (and_14_out, keyboard_1_avail, dipswitch_2_p1);
  Hex_Digit_Display #(.decimalPoint("false")) hex_digit_display_4 (.value(Dl[3:0]));
  not not_2 (not_2_out, and_14_out);
  not not_3 (not_3_out, not_2_out);
  not not_4 (not_4_out, not_3_out);
  Button R (.out(res));
  and and_15 (IRQ, and_14_out, not_4_out);
  LedBar ledbar_1 (
    .led0(Dh[7]), .led1(Dh[6]), .led2(Dh[5]), .led3(Dh[4]), .led4(Dh[3]), .led5(Dh[2]), .led6(Dh[1]),
    .led7(Dh[0]));
  DipSwitch dipswitch_1 (
    .sw1(Bin[7]), .sw2(Bin[6]), .sw3(Bin[5]), .sw4(Bin[4]), .sw5(Bin[3]), .sw6(Bin[2]), .sw7(Bin[1]),
    .sw8(Bin[0]));
  // DipSwitch #(.number(2)) dipswitch_2: pin names not known; wires that end beside it: dipswitch_2_p1, dipswitch_2_p2
  LedBar ledbar_2 (
    .led0(Dl[7]), .led1(Dl[6]), .led2(Dl[5]), .led3(Dl[4]), .led4(Dl[3]), .led5(Dl[2]), .led6(Dl[1]),
    .led7(Dl[0]));
  not not_5 (Enable, dipswitch_2_p2);
  not not_6 (not_6_out, WE);
  and and_16 (and_16_out, not_6_out, C1);
  and and_17 (and_17_out, C1, WE);
  // RGB_Video #(.cursor("No Cursor"), .height(16), .reset("Synchronous"), .scale(8), .width(16)) rgb_video_1: pin names not known; wires that end beside it: and_16_out, CLK, and_17_out, ScreenPos[3:0], ScreenPos[7:4], DATA

  // Notes on the sheet:
  //   contents of rom_2 (hex, n*v repeats v):
  //   90 0 6 0 0 0 40 b0 40 40 a0 9 30 aa 1 f0 ff fc
  //   Enable keboard
  //   Interrupts
  //   Disable CPU
endmodule
