// Logisim project Siliconis_1.circ as structural Verilog: 1 circuit, main circuit main
module main (
);

  wire clock_1_out, demultiplexer_1_out0, demultiplexer_1_out2, demultiplexer_1_out3, demultiplexer_1_out4,
       demultiplexer_2_out1, demultiplexer_2_out2, Int, keyboard_1_avail, kp8b_1_clko, kp8b_1_r_w, not_1_out,
       not_2_out, not_3_out, R_out;
  wire [1:0] kp8b_1_addr_2;
  wire [6:0] keyboard_1_data;
  wire [7:0] bit_extender_1_out, kp8b_1_dout, multiplexer_1_out, multiplexer_2_out, ram_1_dout, register_1_q,
       register_2_q, register_3_q, rom_1_data, undriven, undriven_2, undriven_3;
  wire [13:0] kp8b_1_addr;

  Clock clock_1 (.out(clock_1_out));
  Multiplexer #(.select(2), .width(8)) multiplexer_1 (
    .in0(rom_1_data), .in1(ram_1_dout), .in2(multiplexer_2_out), .out(multiplexer_1_out), .sel(kp8b_1_addr_2));  // open: in3
  Multiplexer #(.select(3), .width(8)) multiplexer_2 (
    .in0({8{1'b0}}), .in1(bit_extender_1_out), .in2(undriven), .in3(undriven_2), .in4(undriven_3),
    .out(multiplexer_2_out), .sel(kp8b_1_addr[2:0]));  // open: in5, in6, in7
  Demultiplexer #(.enable("true"), .select(3)) demultiplexer_1 (
    .out0(demultiplexer_1_out0), .out2(demultiplexer_1_out2), .out3(demultiplexer_1_out3),
    .out4(demultiplexer_1_out4), .in(demultiplexer_2_out2), .sel(kp8b_1_addr[2:0]), .en(demultiplexer_2_out2));  // open: out1, out5, out6, out7
  KP8B kp8b_1 (
    .DIN(multiplexer_1_out), .IRQ(Int), .NMI(1'b0), .RES(R_out), .RDY(1'b1), .CLK(clock_1_out),
    .ADDR({kp8b_1_addr_2, kp8b_1_addr}), .R_W(kp8b_1_r_w), .CLKO(kp8b_1_clko), .DOUT(kp8b_1_dout));  // open: MRB
  Register register_1 (.D(kp8b_1_dout), .en(demultiplexer_1_out2), .clk(kp8b_1_clko), .Q(register_1_q), .clr(R_out));
  Register register_2 (.D(kp8b_1_dout), .en(demultiplexer_1_out3), .clk(kp8b_1_clko), .Q(register_2_q), .clr(R_out));
  Register register_3 (.D(kp8b_1_dout), .en(demultiplexer_1_out4), .clk(kp8b_1_clko), .Q(register_3_q), .clr(R_out));
  Demultiplexer #(.select(2)) demultiplexer_2 (
    .out1(demultiplexer_2_out1), .out2(demultiplexer_2_out2), .in(kp8b_1_r_w), .sel(kp8b_1_addr_2));  // open: out0, out3
  ROM #(.addrWidth(13)) rom_1 (.addr(kp8b_1_addr[12:0]), .data(rom_1_data));
  RAM #(.addrWidth(14), .enables("line")) ram_1 (
    .addr(kp8b_1_addr), .we(demultiplexer_2_out1), .clk(kp8b_1_clko), .din(kp8b_1_dout), .dout(ram_1_dout));
  Button R (.out(R_out));
  TTY tty_1 (.data(kp8b_1_dout[6:0]), .clk(kp8b_1_clko), .we(demultiplexer_1_out0), .clr(R_out));
  Keyboard #(.buflen(1)) keyboard_1 (
    .clk(kp8b_1_clko), .re(1'b1), .clr(R_out), .avail(keyboard_1_avail), .data(keyboard_1_data));
  not not_1 (not_1_out, keyboard_1_avail);
  not not_2 (not_2_out, not_1_out);
  not not_3 (not_3_out, not_2_out);
  and and_1 (Int, not_3_out, keyboard_1_avail);
  assign bit_extender_1_out = {{1{1'b0}}, keyboard_1_data};  // Bit_Extender bit_extender_1

  // Notes on the sheet:
  //   Out
  //   In
endmodule
